# Fritzing sketch fritzing_template (saved by Fritzing 0.9.10b)
breadboards: 1

parts:
  Resistor = Resistor [tolerance=±5% power=0.25 resistance=10k package=THT]
  Photoresistor = Photocell (LDR) [package=THT]
  M5Core-Ink = M5Core-Ink
  Pressure-Sensor = Basic Force Sensing Resistor (FSR) [package=THT]  # not connected
  Solenoid = Solenoid  # not connected
  Infrared-Proximity-Sensor = Infrared Proximity Sensor [distance_to_obstacle=50%]  # not connected
  Ultrasonic-Sensor = HC-SR04 Ultrasonic Distance Sensor  # not connected
  M5Stack-Relay-Unit = relay-unit [package=M5Stack]  # not connected
  M5Stack-RGB-Unit = rgb-led-unit [package=M5Stack]
  Piezo = Piezo Speaker  # not connected
  Servo = Basic Servo  # not connected
  M5Stack-Light-Sensor-Unit = light-sensor-unit [package=M5Stack]

nets:
  N1: Resistor.Pin_0, Photoresistor.pin_1, M5Core-Ink.6_G26
  GND: Resistor.Pin_1, M5Core-Ink.8_GND
  3.3V: Photoresistor.pin_0, M5Core-Ink.2_3V3
  5V: M5Core-Ink.1_5VIN
  N2: M5Core-Ink.9_GND, M5Stack-RGB-Unit.GND-A
  N3: M5Core-Ink.10_5V, M5Stack-RGB-Unit.5V-A
  N4: M5Core-Ink.11_G32, M5Stack-RGB-Unit.OUT-A
  N5: M5Core-Ink.12_G33, M5Stack-RGB-Unit.IN-A
  N6: M5Stack-RGB-Unit.GND-B, M5Stack-Light-Sensor-Unit.GND
  N7: M5Stack-RGB-Unit.5V-B, M5Stack-Light-Sensor-Unit.5V
  N8: M5Stack-RGB-Unit.OUT-B, M5Stack-Light-Sensor-Unit.D.OUT
  N9: M5Stack-RGB-Unit.IN-B, M5Stack-Light-Sensor-Unit.A.OUT

notes:
  Microprocessor (ESP32)
  Inputs (Sensors)
  M5Stack Modules
  Outputs (Actuators)

custom parts:
  M5Core-Ink: M5Stack Core Ink ESP32 Board
  relay-unit: M5Stack Relay Unit (U023)
  rgb-led-unit: M5Stack SK6812 RGB LED Unit (U003)
  light-sensor-unit: M5Stack Light Sensor Unit (U021)
